# Fritzing sketch luci , tapparelle, IR casa (saved by Fritzing 0.9.3b)
breadboards: 1

parts:
  ingresso = RELAY [package=relay-g5q]
  U1 = RELAY [package=relay-g5q]
  cucina-soggiorno = RELAY [package=relay-g5q]
  camera = RELAY [package=relay-g5q]
  ARDUINO_UNO = Arduino Uno (Rev3)
  1 = RELAY [package=relay-t9a]
  U2 = RELAY [package=relay-t9a-2]
  U3 = RELAY [package=relay-g5q]
  bagno = RELAY [package=relay-jzc]  # not connected
  ausiliario_cucina = RELAY [package=relay-g5q]
  tapparella_1 = RELAY [package=relay-g5q]
  tapparella_2 = RELAY [package=relay-g5q]
  U4 = TMP36 [package=to-92-kit]

nets:
  N1: ingresso.COIL2, ausiliario_cucina.COIL1
  N2: ingresso.COIL1, U1.COIL1, ARDUINO_UNO.D10_PWM/SS
  N3: U1.COIL2, cucina-soggiorno.COIL2, camera.COIL2, tapparella_1.COIL1, tapparella_2.COIL1, U4.GND
  N4: cucina-soggiorno.COIL1, ARDUINO_UNO.D12/MISO
  N5: camera.COIL1, ARDUINO_UNO.D13/SCK
  N6: ARDUINO_UNO.A2, U4.VOUT
  N7: ARDUINO_UNO.D8, tapparella_2.COIL2
  N8: ARDUINO_UNO.D9_PWM, ausiliario_cucina.COIL2
  N9: ARDUINO_UNO.D11_PWM/MOSI, 1.COIL1, U2.COIL1, U3.COIL1
  N10: ARDUINO_UNO.D7, tapparella_1.COIL2
  5V: ARDUINO_UNO.5V, U4.VCC
