# Fritzing sketch luci casa (saved by Fritzing 0.9.3b)
breadboards: 1

parts:
  bagno = Momentary Switch [package=ksa_sealed_tac_switch]
  camera = Momentary Switch [package=ksa_sealed_tac_switch]
  ingresso = Momentary Switch [package=ksa_sealed_tac_switch]
  cucina-soggiorno = Momentary Switch [package=ksa_sealed_tac_switch]
  ingresso_2 = RELAY [package=relay-g5q]
  part = RELAY [package=relay-g5q]
  cucina-soggiorno_2 = RELAY [package=relay-g5q]
  camera_2 = RELAY [package=relay-g5q]
  ARDUINO_UNO = Arduino Uno (Rev3)
  1 = RELAY [package=relay-t9a]
  part_2 = RELAY [package=relay-t9a-2]
  part_3 = RELAY [package=relay-g5q]
  bagno_2 = RELAY [package=relay-jzc]  # not connected

nets:
  N1: bagno.1, ARDUINO_UNO.D6_PWM
  N2: camera.1, ARDUINO_UNO.D8
  N3: camera.3, ingresso.3
  N4: camera.4, part.COIL2, cucina-soggiorno_2.COIL2, camera_2.COIL2, ARDUINO_UNO.GND
  N5: ingresso.1, ARDUINO_UNO.D5_PWM
  N6: cucina-soggiorno.1, ARDUINO_UNO.D7
  N7: ingresso_2.COIL1, part.COIL1, ARDUINO_UNO.D10_PWM/SS
  N8: cucina-soggiorno_2.COIL1, ARDUINO_UNO.D12/MISO
  N9: camera_2.COIL1, ARDUINO_UNO.D13/SCK
  N10: ARDUINO_UNO.D11_PWM/MOSI, 1.COIL1, part_2.COIL1, part_3.COIL1
